# Fritzing sketch schematic (saved by Fritzing 1.0.6)

parts:
  U2 = ESP32-38PinWide [part_number=ESP32-38PinWide]
  LCD2004-I2C1 = LCD2004-I2C [mn=xxx]
  Mod1 = zmpt101b
  A1 = 2x18650 battery shield [package=THT]
  S1 = Square Pushbutton
  S2 = Square Pushbutton
  S3 = Square Pushbutton
  M1 = AC-05-03
  J2 = Camdenboss CTB0158-3 [part_number=CTB0158-3 package=THT]
  MOD1 = MT3608 Boost No usb
  R1 = Resistor [tolerance=±5% power=0.25W resistance=1000 package=THT]
  R2 = Resistor [tolerance=±5% power=0.25W resistance=3000 package=THT]
  J1 = Piezo Speaker

nets:
  N1: U2.GPIO35, R1.Pin_1, R2.Pin_0
  N2: U2.GPIO25, J1.pin2
  N3: U2.GPIO11, LCD2004-I2C1.GND, Mod1.GND#2, A1.pin_2, A1.pin_8, A1.pin_10, A1.pin_11, A1.pin_13, A1.Pin_19, S1.leg1, S2.leg1, S3.leg1, M1.pin_4, MOD1.IN_(-), MOD1.OUT_(-), R1.Pin_0, J1.pin1
  VIN: U2.VIN, LCD2004-I2C1.VCC, A1.pin_1, A1.pin_7, A1.pin_9, M1.pin_3, MOD1.IN_(+)
  N4: U2.GPIO18, S3.leg0
  N5: U2.GPIO19, S2.leg0
  N6: U2.GPIO21, LCD2004-I2C1.SDA
  N7: U2.GPIO22, LCD2004-I2C1.SCL
  N8: U2.GPIO23, S1.leg0
  N9: Mod1.VCC, MOD1.OUT_(+)
  N10: Mod1.OUT, R2.Pin_1
  N11: Mod1.GND#3, J2.pin2
  N12: Mod1.N, M1.pin_2, J2.pin1
  N13: Mod1.L, M1.pin_1, J2.pin3

notes:
  UP
  CLEAR
  DOWN
  GRID

custom parts:
  ESP32-38PinWide: Generic 38-Pin ESP32 with wide format (only access to one side of pins on a breadboard) based on Stephen Lilley's HiLetgo ESP-WROOM-32 ESP32 ESP-32S Development Board.
  LCD2004-I2C: A standard character display with 4x20 characters. Comes in many colors with LCM2004 IIC attached.
  zmpt101b: Single phase ac active output voltate transformer module.
  2x18650 battery shield: 2x18650 Lithium Battery Shield V9 CC CV Type-C Micro USB Mobile Power Bank DIY Module 5V 3A 3V 1A for iPhone Samsung Xiaomi.
  AC-05-03: AC-DC 220V to 5V Step-Down Power Supply Module
  MT3608 Boost No usb: Chip- MT3608 / B6289 DC to DC step up, power booster module. With adjustable output voltage. Current- 2A . || Input voltage- 2V-24V || Output voltage- 5V-28V Input interface- Inversed polarity- NO. || Led indicator- No.
